// Logisim project processor.circ as structural Verilog
module EX (
  input  [31:0] A,
  input  [31:0] B,
  input  [31:0] imm,
  input  [4:0] Sa,
  input  [31:0] PC_4,
  input  [31:0] ctrl,
  output [31:0] D,
  output [31:0] Bout,
  output [31:0] ctrlout
);

  wire [31:0] multiplexer_1_out;

  Multiplexer #(.width(32), .enable("false")) multiplexer_1 (.in0(B), .in1(imm), .out(multiplexer_1_out));  // open: sel
  // Mips_ALU mips_alu_1: pin names not known; wires that end beside it: A, multiplexer_1_out, Sa, D

  assign Bout = B;
  assign ctrlout = ctrl;
endmodule

module IF (
  input  Clock,
  output [31:0] inst,
  output [31:0] out_3
);

  wire [31:0] incrementer_1_p3;

  // Incrementer incrementer_1: pin names not known; wires that end beside it: incrementer_1_p3[31:2], out_3[31:2], incrementer_1_p3
  Register #(.width(32)) register_1 (.D({out_3[31:2], 2'b00}), .Q(incrementer_1_p3), .clk(Clock));  // open: en, clr
  // MIPSProgramROM mipsprogramrom_1: pin names not known; wires that end beside it: inst

  assign out_3[1:0] = 2'b00;

  // Other names for the same wires on the sheet: tPC_4[31:2] = out_3[31:2]
endmodule

module MEM (
  input  [31:0] D,
  input  [31:0] B,
  input  [31:0] ctrl,
  output [31:0] Dout,
  output [31:0] M,
  output [31:0] ctrlout
);


  assign ctrlout = ctrl;
  assign Dout = D;
  assign M = {32{1'b0}};
endmodule

module WB (
  input  [31:0] D,
  input  [31:0] M
);
endmodule

module ID (
  input  [31:0] inst,
  input  [31:0] PC_4,
  output [31:0] A,
  output [31:0] B,
  output [31:0] imm,
  output [31:0] PC_4out,
  output [31:0] ctrl
);

  // RegisterFile registerfile_1: pin names not known; wires that end beside it: A, B
  Bit_Extender bit_extender_1 ();  // open: in, out
endmodule
